# Fritzing sketch FirstDevelpopingSchematic (saved by Fritzing 0.8.5b)
breadboards: 1

parts:
  Arduino1 = Arduino Mini (Rev5)
  R1 = Rotary Potentiometer (Small) [maximum_resistance=100kΩ package=THT]
  NEOPIXEL1 = Neopixel Strip -- Black (30/m)
  MIC1 = MAX4466 Electret Microphone Breakout Board

nets:
  N1: Arduino1.D6_PWM, NEOPIXEL1.DO
  N2: Arduino1.D9_PWM, MIC1.out
  N3: Arduino1.A2, R1.wiper
  GND: Arduino1.GND, NEOPIXEL1.GND, MIC1.GND
  5V: Arduino1.5V, R1.leg1, R1.leg2, NEOPIXEL1.+5V, MIC1.VCC

custom parts:
  Neopixel Strip -- Black (30/m): Neopixel Strip, Black, 30 pixels per meter.
  MAX4466 Electret Microphone Breakout Board: MAX4466 Electrec Microphone Breakout Board
